// Logisim project nikola.circ as structural Verilog: 1 circuit, main circuit main
module main (
  input  in_1,
  input  in_2,
  output out_3
);

  wire not_1_out, or_1_out;

  // Probe on or_1_out
  or or_1 (or_1_out, in_2, in_1);
  not not_1 (not_1_out, in_1);
  nand nand_1 (out_3, or_1_out, not_1_out);
  // Probe on out_3
endmodule
